// Logisim project lab4_n_plus_4.circ as structural Verilog: 1 circuit, main circuit main
module main (
  input  [3:0] in_1,
  output [3:0] out_2,
  output out_3,
  output out_4,
  output out_5,
  output out_6
);

  wire and_1_out, and_2_out, and_3_out, and_4_out, and_6_out, and_7_out, not_1_out, not_2_out, not_3_out,
       not_4_out;

  // Probe on in_1
  not not_1 (not_1_out, in_1[0]);
  not not_2 (not_2_out, in_1[1]);
  not not_3 (not_3_out, in_1[2]);
  not not_4 (not_4_out, in_1[3]);
  and and_1 (and_1_out, in_1[2], not_4_out);
  or or_1 (out_2[3], and_1_out, and_2_out);
  and and_2 (and_2_out, in_1[3], not_3_out, not_2_out);
  and and_3 (and_3_out, not_4_out, not_3_out);
  or or_2 (out_2[2], and_3_out, and_4_out);
  and and_4 (and_4_out, not_3_out, not_2_out);
  and and_5 (out_2[1], in_1[1], not_4_out);
  and and_6 (and_6_out, in_1[0], not_4_out);
  or or_3 (out_2[0], and_6_out, and_7_out);
  and and_7 (and_7_out, in_1[0], not_3_out, not_2_out);
  // Probe on out_2

  assign out_3 = out_2[3];
  assign out_4 = out_2[2];
  assign out_5 = out_2[1];
  assign out_6 = out_2[0];

  // Notes on the sheet:
  //   A
  //   D
  //   B
  //   C
  //   !A
  //   !B
  //   !C
  //   !D
endmodule
