// Logisim project lab5.circ as structural Verilog: 1 circuit, main circuit main
module main (
  input  in_1,
  input  in_2
);

  wire clock_1_out, nand_1_out, nand_2_out, nand_3_out, nand_4_out, nand_5_out, nand_6_out, nand_7_out,
       nand_8_out, nand_9_out, nand_10_out;
  wire [2:0] t_ff_3_q;

  // Probe on t_ff_3_q
  Clock clock_1 (.out(clock_1_out));
  T_Flip_Flop t_ff_1 (.clk(clock_1_out), .T(nand_10_out), .Q(t_ff_3_q[2]));  // open: Qn, preset, reset
  T_Flip_Flop t_ff_2 (.clk(clock_1_out), .T(nand_2_out), .Q(t_ff_3_q[1]));  // open: Qn, preset, reset
  T_Flip_Flop t_ff_3 (.clk(clock_1_out), .T(in_2), .Q(t_ff_3_q[0]));  // open: Qn, preset, reset
  nand nand_1 (nand_1_out, nand_8_out, in_2);
  nand nand_2 (nand_2_out, nand_1_out, nand_6_out);
  nand nand_3 (nand_3_out, t_ff_3_q[0], t_ff_3_q[0]);
  nand nand_4 (nand_4_out, nand_7_out, nand_7_out);
  nand nand_5 (nand_5_out, in_2, nand_4_out, nand_8_out);
  nand nand_6 (nand_6_out, nand_8_out, in_2);
  nand nand_7 (nand_7_out, t_ff_3_q[1], t_ff_3_q[1]);
  nand nand_8 (nand_8_out, nand_3_out, nand_3_out);
  nand nand_9 (nand_9_out, in_2, nand_8_out, nand_4_out);
  nand nand_10 (nand_10_out, nand_5_out, nand_9_out);

  // Notes on the sheet:
  //   C
  //   B
  //   A
  //   !B
  //   !A
  //   B
  //   A
endmodule
